// Logisim project 1_1_NOTgatedelay.circ as structural Verilog: 1 circuit, main circuit main
module main (
);

  wire clock_1_out, ic_7404_1_p2;

  Clock clock_1 (.out(clock_1_out));
  // IC_7404 ic_7404_1: pin names not known; wires that end beside it: clock_1_out, ic_7404_1_p2
  // Probe on ic_7404_1_p2
endmodule
