// Logisim project 1_2_ORgatedelay.circ as structural Verilog: 1 circuit, main circuit main
module main (
);

  wire clock_1_out, ic_7432_1_p3;

  Clock clock_1 (.out(clock_1_out));
  // Probe on ic_7432_1_p3
  // IC_7432 ic_7432_1: pin names not known; wires that end beside it: clock_1_out, 1'b0, ic_7432_1_p3
endmodule
