// Logisim project 2_1_RisingEdgeDetec.circ as structural Verilog: 1 circuit, main circuit main
module main (
);

  wire clock_1_out, ic_7404_1_p2, ic_7404_1_p3, ic_7404_1_p4, ic_7404_1_p8, ic_7432_1_p3;

  Clock clock_1 (.out(clock_1_out));
  // IC_7404 ic_7404_1: pin names not known; wires that end beside it: clock_1_out, ic_7404_1_p2, ic_7404_1_p3, ic_7404_1_p4, ic_7404_1_p2, ic_7404_1_p3, ic_7404_1_p4, ic_7404_1_p8
  // Probe on ic_7432_1_p3
  // IC_7432 ic_7432_1: pin names not known; wires that end beside it: ic_7404_1_p2, ic_7404_1_p8, ic_7432_1_p3

  // Notes on the sheet:
  //   CLK - Probe input
  //   Probe output
endmodule
