// Logisim project 2_1_RisingEdgeDetecDFF.circ as structural Verilog: 1 circuit, main circuit main
module main (
);

  wire clock_1_out, d_ff_1_q, d_ff_1_qn, ic_7404_1_p2, ic_7404_1_p3, ic_7404_1_p4, ic_7404_1_p8, ic_7432_1_p3;

  Clock clock_1 (.out(clock_1_out));
  // IC_7404 ic_7404_1: pin names not known; wires that end beside it: clock_1_out, ic_7404_1_p2, ic_7404_1_p3, ic_7404_1_p4, ic_7404_1_p2, ic_7404_1_p3, ic_7404_1_p4, ic_7404_1_p8
  // IC_7432 ic_7432_1: pin names not known; wires that end beside it: ic_7404_1_p2, ic_7404_1_p8, ic_7432_1_p3
  D_Flip_Flop d_ff_1 (.clk(ic_7432_1_p3), .D(d_ff_1_qn), .Q(d_ff_1_q), .Qn(d_ff_1_qn));  // open: preset, en, reset
  // Probe on d_ff_1_q

  // Notes on the sheet:
  //   CLK - Probe input
  //   Probe output
endmodule
