// Logisim project 2_2_FallingEdgeDetec.circ as structural Verilog: 1 circuit, main circuit main
module main (
);

  wire clock_1_out, ic_7404_1_p2, ic_7404_1_p3, ic_7404_1_p6, ic_7432_1_p2;

  Clock clock_1 (.out(clock_1_out));
  // IC_7404 ic_7404_1: pin names not known; wires that end beside it: clock_1_out, ic_7404_1_p2, ic_7404_1_p3, ic_7404_1_p2, ic_7404_1_p3, ic_7404_1_p6, ic_7404_1_p6
  // Probe on ic_7432_1_p2
  // IC_7432 ic_7432_1: pin names not known; wires that end beside it: clock_1_out, ic_7432_1_p2
endmodule
