// Logisim project ex1.circ as structural Verilog: 1 circuit, main circuit main
module main (
);

  wire clock_1_out, ic_7404_1_p2, ic_7473_1_p5, ic_7473_1_p6;

  Clock clock_1 (.out(clock_1_out));
  // IC_7404 ic_7404_1: pin names not known; wires that end beside it: 1'b1, ic_7404_1_p2
  // IC_7473 ic_7473_1: pin names not known; wires that end beside it: 1'b1, clock_1_out, ic_7404_1_p2, 1'b1, ic_7473_1_p5, ic_7473_1_p6
  // Probe on ic_7473_1_p5
  // Probe on ic_7473_1_p6

  // Notes on the sheet:
  //   D
  //   CLR1
  //   Q
  //   Q'
endmodule
