// Logisim project ex2.2.circ as structural Verilog: 1 circuit, main circuit main
module main (
);

  wire clock_1_out, ic_7474_1_p1, ic_7474_1_p3, ic_7474_1_p4, ic_7474_1_p11, ic_7474_2_p1, ic_7474_2_p3,
       ic_7474_2_p4;

  Clock clock_1 (.out(clock_1_out));
  // IC_7474 ic_7474_1: pin names not known; wires that end beside it: ic_7474_1_p1, clock_1_out, ic_7474_1_p3, ic_7474_1_p4, 1'b1, 1'b1, 1'b1, 1'b1, ic_7474_1_p4, ic_7474_1_p1, ic_7474_1_p11, ic_7474_1_p3
  // Probe on ic_7474_2_p1
  // Probe on ic_7474_1_p1
  // Probe on ic_7474_1_p3
  // Probe on ic_7474_2_p3
  // IC_7474 ic_7474_2: pin names not known; wires that end beside it: ic_7474_2_p1, ic_7474_1_p11, ic_7474_2_p3, ic_7474_2_p4, 1'b1, 1'b1, 1'b1, 1'b1, ic_7474_2_p4, ic_7474_2_p1, ic_7474_2_p3

  // Notes on the sheet:
  //   QA
  //   QB
  //   QC
  //   QD
endmodule
