// Logisim project ex3.circ as structural Verilog: 1 circuit, main circuit main
module main (
);

  wire and_1_out, clock_1_out, d_ff_1_q, d_ff_1_qn, j_k_ff_1_q, j_k_ff_1_qn, not_1_out, not_2_out, or_1_out;

  Clock clock_1 (.out(clock_1_out));
  not not_1 (not_1_out, 1'b1);
  not not_2 (not_2_out, 1'b1);
  D_Flip_Flop #(.trigger("falling")) d_ff_1 (
    .clk(clock_1_out), .D(and_1_out), .Q(d_ff_1_q), .Qn(d_ff_1_qn), .preset(not_1_out), .reset(not_2_out));  // open: en
  and and_1 (and_1_out, 1'b1, j_k_ff_1_q);
  // Probe on d_ff_1_q
  // Probe on j_k_ff_1_q
  J_K_Flip_Flop #(.trigger("falling")) j_k_ff_1 (
    .J(d_ff_1_qn), .clk(clock_1_out), .K(d_ff_1_q), .Q(j_k_ff_1_q), .Qn(j_k_ff_1_qn), .preset(not_1_out),
    .reset(not_2_out));  // open: en
  or or_1 (or_1_out, d_ff_1_qn, j_k_ff_1_qn);
  // Probe on or_1_out

  // Notes on the sheet:
  //   x
  //   CLK
  //   PRE'
  //   CLR'
  //   Z
endmodule
